# Fritzing sketch Nano_ESP32-PCB_Smal-V03 (saved by Fritzing 1.0.3b)
circuit board: 3.1194cm x 12.0239cm

parts:
  74AHCT125 = 74HC08 Logic AND Gate [part_number=74HC08 package="DIP (Dual Inline) [THT]"]
  C1 = Electrolytic Capacitor [capacitance=1mF voltage=35V package="100 mil [THT, electrolytic]"]
  Arduino_Nano_ESP32 = Arduino Nano (Rev3.0)
  RTCclock7 = female pin header, 3 pins [form="♀ (female)"]
  R14 = Resistor [tolerance=±5% resistance=470 power=0.25 package=THT]
  J2 = screw terminal, 2 pins
  RTC-clock = female pin header, 6 pins [form="♀ (female)"]
  LDR = male pin header, 2 pins [form="♂ (male)"]
  R15 = Resistor [tolerance=±5% resistance=10k power=0.25W package=THT]
  1N5818 = Rectifier Diode [part_number=1N4001 package="300 mil [THT]"]
  Rotary = female pin header, 5 pins [form="♀ (female)"]

nets:
  N1: 74AHCT125.1A, C1.-, Arduino_Nano_ESP32.GND, RTCclock7.pin3, J2.pin1, RTC-clock.pin1, R15.Pin_1, Rotary.pin1
  N2: 74AHCT125.1B, Arduino_Nano_ESP32.D5
  N3: 74AHCT125.1Y, R14.Pin_0
  N4: 74AHCT125.VCC, C1.+, RTCclock7.pin1, J2.pin2, 1N5818.anode
  N5: Arduino_Nano_ESP32.D2, Rotary.pin5
  N6: Arduino_Nano_ESP32.D3, Rotary.pin4
  N7: Arduino_Nano_ESP32.D4, Rotary.pin3
  N8: Arduino_Nano_ESP32.5V, 1N5818.cathode
  N9: Arduino_Nano_ESP32.A5, RTC-clock.pin4
  N10: Arduino_Nano_ESP32.A4, RTC-clock.pin3
  N11: Arduino_Nano_ESP32.A2, LDR.pin2, R15.Pin_0
  N12: Arduino_Nano_ESP32.3V3, RTC-clock.pin2, LDR.pin1, Rotary.pin2
  N13: RTCclock7.pin2, R14.Pin_1

notes:
  +
  -
  Gnd
  32K
  SQW
  SCL
  SDA
  3V3
  Power
  5V
  A5
  A4
  D5
  A3
  A2
  TX
  RX
  DT
  SW
  CLK
  D6
  D8
  D9
  D10
  D11
  D12
  A1
  A6
  A7
  Vin
  Rst
  D4
  D3
  D2
  A0
  Aref
  D13
  Signal
  USB
  D7
  Ed Nieuwenhuys 2024
  USB side
  wire or
